# Fritzing sketch Automated_Home (saved by Fritzing 0.9.3b)
breadboards: 1

parts:
  Part1 = Arduino Uno (Rev3)
  U1 = Voltage Regulator - 3.3V [package="TO220 [THT]"]
  C1 = Capacitor Polarized [package=cpol-radial-10uf-25v]
  R1 = Resistor [tolerance=±5% resistance=220 package=THT]
  LED1 = LED - 5mm [color="Red (633nm)" package="5 mm [THT]"]
  U2 = ESP8266 WiFi Module [part_number=ESP8266]
  U3 = RELAY [package=OJ]
  IC1 = ULN2803A [package=THT]
  D2 = Rectifier Diode [part_number=1N4001 package="300 mil [THT]"]  # not connected
  D3 = Rectifier Diode [part_number=1N4001 package="300 mil [THT]"]  # not connected
  D4 = Rectifier Diode [part_number=1N4001 package="300 mil [THT]"]  # not connected
  D1 = Rectifier Diode [part_number=1N4001 package="300 mil [THT]"]

nets:
  N1: Part1.D10_PWM/SS, IC1.In_4
  N2: Part1.D11_PWM/MOSI, IC1.In_3
  N3: Part1.D12/MISO, IC1.In_2
  N4: Part1.D13/SCK, IC1.In_1
  GND: Part1.GND, U1.GND, C1.-, LED1.cathode, U2.GND, U3.MAIN, IC1.0V, D1.cathode
  N5: Part1.D4, U2.RXD
  N6: Part1.D5_PWM, U2.TXD
  N7: Part1.5V, U1.input_voltage, IC1.COM_-_Common
  N8: U1.output_voltage, C1.+, R1.Pin_0, U2.VCC, U2.CH_PD
  N9: R1.Pin_1, LED1.anode
  N10: U3.NO, IC1.Out_1, D1.anode
